// Logisim project F1.circ as structural Verilog: 1 circuit, main circuit main
module main (
  input  A,
  input  B,
  input  C,
  input  D,
  input  A_2,
  input  B_2,
  input  C_2,
  input  D_2,
  output F1,
  output F1_2
);

  wire and_1_out, nand_1_out, not_1_out, not_2_out, not_3_out, not_4_out, not_5_out, not_6_out, not_7_out,
       not_8_out, not_9_out;

  not not_1 (not_1_out, B);
  not not_2 (not_2_out, D);
  not not_3 (not_3_out, B_2);
  not not_4 (not_4_out, D_2);
  and and_1 (and_1_out, A, not_1_out, not_2_out);
  nand nand_1 (nand_1_out, A_2, not_3_out, not_4_out);
  not not_5 (not_5_out, nand_1_out);
  not not_6 (not_6_out, C_2);
  or or_1 (F1, and_1_out, not_7_out);
  not not_7 (not_7_out, C);
  not not_8 (not_8_out, not_5_out);
  not not_9 (not_9_out, not_6_out);
  nand nand_2 (F1_2, not_8_out, not_9_out);
endmodule
