// Logisim project F2.circ as structural Verilog: 1 circuit, main circuit main
module main (
  input  A,
  input  B,
  input  C,
  input  D,
  input  A_2,
  input  B_2,
  input  C_2,
  input  D_2,
  output F2,
  output F2_2
);

  wire and_1_out, and_2_out, and_3_out, nand_1_out, nand_2_out, nand_3_out, not_1_out, not_2_out, not_3_out,
       not_4_out, not_5_out, not_6_out, not_7_out, not_8_out;

  and and_1 (and_1_out, A, not_1_out);
  not not_1 (not_1_out, B);
  and and_2 (and_2_out, B, D);
  and and_3 (and_3_out, C, D);
  nand nand_1 (nand_1_out, A_2, not_2_out);
  not not_2 (not_2_out, B_2);
  nand nand_2 (nand_2_out, B_2, D_2);
  nand nand_3 (nand_3_out, C_2, D_2);
  not not_3 (not_3_out, nand_1_out);
  not not_4 (not_4_out, nand_2_out);
  not not_5 (not_5_out, nand_3_out);
  or or_1 (F2, and_1_out, and_2_out, and_3_out);
  not not_6 (not_6_out, not_3_out);
  not not_7 (not_7_out, not_4_out);
  not not_8 (not_8_out, not_5_out);
  nand nand_4 (F2_2, not_6_out, not_7_out, not_8_out);
endmodule
