// Logisim project Q2.circ as structural Verilog: 2 circuits, main circuit main
module main (
  input  A,
  input  B,
  input  C,
  input  D,
  input  A_2,
  input  B_2,
  input  C_2,
  input  D_2,
  output F,
  output F_2
);

  wire and_1_out, and_2_out, and_3_out, nand_1_out, nand_2_out, nand_3_out, not_1_out, not_2_out, not_3_out,
       not_4_out, not_5_out, not_6_out, not_7_out, not_8_out, not_9_out, not_10_out;

  not not_1 (not_1_out, B);
  not not_2 (not_2_out, D);
  not not_3 (not_3_out, B_2);
  not not_4 (not_4_out, D_2);
  and and_1 (and_1_out, A, D);
  and and_2 (and_2_out, B, C);
  and and_3 (and_3_out, not_1_out, not_2_out);
  nand nand_1 (nand_1_out, A_2, D_2);
  not not_5 (not_5_out, nand_1_out);
  not not_6 (not_6_out, nand_2_out);
  nand nand_2 (nand_2_out, B_2, C_2);
  nand nand_3 (nand_3_out, not_3_out, not_4_out);
  not not_7 (not_7_out, nand_3_out);
  or or_1 (F, and_1_out, and_2_out, and_3_out);
  not not_8 (not_8_out, not_5_out);
  not not_9 (not_9_out, not_6_out);
  not not_10 (not_10_out, not_7_out);
  nand nand_4 (F_2, not_8_out, not_9_out, not_10_out);
endmodule

module F (
  input  A,
  input  B,
  input  C,
  input  D,
  input  A_2,
  input  B_2,
  input  C_2,
  input  D_2,
  output F_prime,
  output F_prime_2
);

  wire and_1_out, and_2_out, and_3_out, nand_1_out, nand_2_out, nand_3_out, not_1_out, not_2_out, not_3_out,
       not_4_out, not_5_out, not_6_out, not_7_out, not_8_out, not_9_out, not_10_out, not_11_out, not_12_out,
       not_13_out, not_14_out, not_15_out, not_16_out, not_17_out, not_18_out;

  and and_1 (and_1_out, B, not_1_out, not_2_out);
  not not_1 (not_1_out, C);
  not not_2 (not_2_out, D);
  not not_3 (not_3_out, A);
  and and_2 (and_2_out, not_3_out, not_4_out, D);
  not not_4 (not_4_out, C);
  not not_5 (not_5_out, A);
  not not_6 (not_6_out, B);
  and and_3 (and_3_out, not_5_out, not_6_out, D);
  not not_7 (not_7_out, C_2);
  nand nand_1 (nand_1_out, B_2, not_7_out, not_8_out);
  not not_8 (not_8_out, D_2);
  not not_9 (not_9_out, A_2);
  not not_10 (not_10_out, C_2);
  nand nand_2 (nand_2_out, not_9_out, not_10_out, D_2);
  not not_11 (not_11_out, A_2);
  not not_12 (not_12_out, B_2);
  nand nand_3 (nand_3_out, not_11_out, not_12_out, D_2);
  not not_13 (not_13_out, nand_1_out);
  not not_14 (not_14_out, nand_2_out);
  not not_15 (not_15_out, nand_3_out);
  or or_1 (F_prime, and_1_out, and_2_out, and_3_out);
  not not_16 (not_16_out, not_13_out);
  not not_17 (not_17_out, not_14_out);
  not not_18 (not_18_out, not_15_out);
  nand nand_4 (F_prime_2, not_16_out, not_17_out, not_18_out);
endmodule
