// Logisim project circuit.circ as structural Verilog: 3 circuits, main circuit main
module main (
  input  a,
  output x,
  output y,
  output z
);

  wire clock_1_out, combinational_circuit_1_n0, combinational_circuit_1_n1, combinational_circuit_1_n2;

  Clock clock_1 (.out(clock_1_out));
  combinational_circuit combinational_circuit_1 (
    .a(a), .R2(x), .R1(y), .R0(z), .N2(combinational_circuit_1_n2), .N1(combinational_circuit_1_n1),
    .N0(combinational_circuit_1_n0));
  _3bit_register u_3bit_register_1 (
    .clock(clock_1_out), .N2(combinational_circuit_1_n2), .N1(combinational_circuit_1_n1),
    .N0(combinational_circuit_1_n0), .R2___x(x), .R1___y(y), .R0___z(z));

  // Notes on the sheet:
  //   clock
  //   combinational circuit
  //   register
endmodule

module _3bit_register (
  input  clock,
  input  N2,
  input  N1,
  input  N0,
  output R2___x,
  output R1___y,
  output R0___z
);

  D_Flip_Flop d_ff_1 (.clk(clock), .D(N2), .Q(R2___x));  // open: Qn, preset, en, reset
  D_Flip_Flop d_ff_2 (.clk(clock), .D(N1), .Q(R1___y));  // open: Qn, preset, en, reset
  D_Flip_Flop d_ff_3 (.clk(clock), .D(N0), .Q(R0___z));  // open: Qn, preset, en, reset
endmodule

module combinational_circuit (
  input  a,
  input  R2,
  input  R1,
  input  R0,
  output N2,
  output N1,
  output N0
);

  wire and_1_out, and_2_out, and_3_out, and_4_out, and_5_out, and_6_out, and_7_out, and_8_out, and_9_out,
       not_1_out, not_2_out, not_3_out, not_4_out, not_5_out, not_6_out, not_7_out, not_8_out, not_9_out,
       not_10_out;

  not not_1 (not_1_out, a);
  not not_2 (not_2_out, R2);
  not not_3 (not_3_out, R1);
  not not_4 (not_4_out, a);
  not not_5 (not_5_out, R2);
  not not_6 (not_6_out, R1);
  not not_7 (not_7_out, R0);
  not not_8 (not_8_out, R2);
  not not_9 (not_9_out, R2);
  not not_10 (not_10_out, a);
  and and_1 (and_1_out, not_1_out, R2);
  and and_2 (and_2_out, not_2_out, a, R0);
  and and_3 (and_3_out, R2, not_3_out, R0);
  and and_4 (and_4_out, R1, R0);
  and and_5 (and_5_out, R1, not_4_out);
  and and_6 (and_6_out, not_5_out, not_6_out, not_7_out, a);
  and and_7 (and_7_out, not_8_out, a);
  and and_8 (and_8_out, not_9_out, R0);
  and and_9 (and_9_out, R0, not_10_out);
  or or_1 (N2, and_1_out, and_2_out, and_3_out);
  or or_2 (N1, and_4_out, and_5_out, and_6_out);
  or or_3 (N0, and_7_out, and_8_out, and_9_out);
endmodule
