// Logisim project Circuit.circ as structural Verilog: 4 circuits, main circuit main
module main (
  input  I0,
  input  I1,
  input  I2,
  input  I3,
  input  I4,
  input  I5,
  input  cl,
  input  ld,
  input  sw,
  output Q0,
  output Q1,
  output Q2,
  output Q3,
  output Q4,
  output Q5
);

  wire combinational_1_s0, combinational_1_s1;

  combinational combinational_1 (.cl(cl), .ld(ld), .sw(sw), .s1(combinational_1_s1), .s0(combinational_1_s0));
  register register_1 (
    .I0(I0), .I1(I1), .I2(I2), .I3(I3), .I4(I4), .I5(I5), .s1(combinational_1_s1), .s0(combinational_1_s0),
    .Q0(Q0), .Q1(Q1), .Q2(Q2), .Q3(Q3), .Q4(Q4), .Q5(Q5));
endmodule

module _2_bit_to_1_bit (
  input  s1,
  input  s0,
  output [1:0] out_3
);

  BitAdder #(.width(1)) bitadder_1 (.in0(s1), .in1(s1), .in2(s0), .out(out_3));
endmodule

module register (
  input  I0,
  input  I1,
  input  I2,
  input  I3,
  input  I4,
  input  I5,
  input  s1,
  input  s0,
  output Q0,
  output Q1,
  output Q2,
  output Q3,
  output Q4,
  output Q5
);

  wire clock_1_out, multiplexer_1_out, multiplexer_2_out, multiplexer_3_out, multiplexer_4_out,
       multiplexer_5_out, multiplexer_6_out;
  wire [1:0] n2_bit_to_1_bit_1_out_3;

  Clock clock_1 (.out(clock_1_out));
  _2_bit_to_1_bit u_2_bit_to_1_bit_1 (.s1(s1), .s0(s0), .out_3(n2_bit_to_1_bit_1_out_3));
  Multiplexer #(.select(2), .enable("false")) multiplexer_1 (
    .in0(multiplexer_1_out), .in1(I0), .in2(1'b0), .in3(Q1), .out(multiplexer_1_out),
    .sel(n2_bit_to_1_bit_1_out_3));
  Multiplexer #(.select(2), .enable("false")) multiplexer_2 (
    .in0(multiplexer_2_out), .in1(I1), .in2(1'b0), .in3(Q0), .out(multiplexer_2_out),
    .sel(n2_bit_to_1_bit_1_out_3));
  Multiplexer #(.select(2), .enable("false")) multiplexer_3 (
    .in0(multiplexer_3_out), .in1(I2), .in2(1'b0), .in3(Q3), .out(multiplexer_3_out),
    .sel(n2_bit_to_1_bit_1_out_3));
  Multiplexer #(.select(2), .enable("false")) multiplexer_4 (
    .in0(multiplexer_4_out), .in1(I3), .in2(1'b0), .in3(Q2), .out(multiplexer_4_out),
    .sel(n2_bit_to_1_bit_1_out_3));
  Multiplexer #(.select(2), .enable("false")) multiplexer_5 (
    .in0(multiplexer_5_out), .in1(I4), .in2(1'b0), .in3(Q5), .out(multiplexer_5_out),
    .sel(n2_bit_to_1_bit_1_out_3));
  Multiplexer #(.select(2), .enable("false")) multiplexer_6 (
    .in0(multiplexer_6_out), .in1(I5), .in2(1'b0), .in3(Q4), .out(multiplexer_6_out),
    .sel(n2_bit_to_1_bit_1_out_3));
  D_Flip_Flop d_ff_1 (.clk(clock_1_out), .D(multiplexer_1_out), .Q(Q0));  // open: Qn, preset, en, reset
  D_Flip_Flop d_ff_2 (.clk(clock_1_out), .D(multiplexer_2_out), .Q(Q1));  // open: Qn, preset, en, reset
  D_Flip_Flop d_ff_3 (.clk(clock_1_out), .D(multiplexer_3_out), .Q(Q2));  // open: Qn, preset, en, reset
  D_Flip_Flop d_ff_4 (.clk(clock_1_out), .D(multiplexer_4_out), .Q(Q3));  // open: Qn, preset, en, reset
  D_Flip_Flop d_ff_5 (.clk(clock_1_out), .D(multiplexer_5_out), .Q(Q4));  // open: Qn, preset, en, reset
  D_Flip_Flop d_ff_6 (.clk(clock_1_out), .D(multiplexer_6_out), .Q(Q5));  // open: Qn, preset, en, reset

  // Notes on the sheet:
  //   clock
endmodule

module combinational (
  input  cl,
  input  ld,
  input  sw,
  output s1,
  output s0
);

  wire and_1_out, and_2_out, not_1_out, not_2_out, not_3_out;

  not not_1 (not_1_out, cl);
  and and_1 (and_1_out, not_1_out, ld);
  not not_2 (not_2_out, cl);
  not not_3 (not_3_out, ld);
  and and_2 (and_2_out, not_2_out, not_3_out, sw);
  or or_1 (s1, and_1_out, cl);
  or or_2 (s0, and_2_out, cl);
endmodule
