// Logisim project 1801042673.circ as structural Verilog: 10 circuits, main circuit main1
module main (
  input  w,
  input  x,
  input  y,
  input  z,
  output out_5
);

  wire not_1_out, not_2_out, not_3_out, not_4_out;

  not not_1 (not_1_out, w);
  not not_2 (not_2_out, x);
  and and_1 (out_5, not_1_out, not_2_out, not_3_out, not_4_out);
  not not_3 (not_3_out, y);
  not not_4 (not_4_out, z);
endmodule

module w_x_y_z (
  input  w,
  input  x,
  input  y,
  input  z,
  output out_5
);

  wire not_1_out, not_2_out;

  not not_1 (not_1_out, w);
  not not_2 (not_2_out, x);
  and and_1 (out_5, not_1_out, not_2_out, y, z);
endmodule

module w_x_yz (
  input  w,
  input  x,
  input  y,
  input  z,
  output out_5
);

  wire not_1_out, not_2_out;

  not not_1 (not_1_out, w);
  and and_1 (out_5, not_1_out, x, not_2_out, z);
  not not_2 (not_2_out, y);
endmodule

module w_xy_z (
  input  w,
  input  x,
  input  y,
  input  z,
  output out_5
);

  wire not_1_out, not_2_out;

  not not_1 (not_1_out, w);
  and and_1 (out_5, not_1_out, x, y, not_2_out);
  not not_2 (not_2_out, z);
endmodule

module w_xyz (
  input  w,
  input  x,
  input  y,
  input  z,
  output out_5
);

  wire not_1_out, not_2_out;

  not not_1 (not_1_out, x);
  and and_1 (out_5, w, not_1_out, not_2_out, z);
  not not_2 (not_2_out, y);
endmodule

module wx_y_z (
  input  w,
  input  x,
  input  y,
  input  z,
  output out_5
);

  wire not_1_out, not_2_out;

  not not_1 (not_1_out, x);
  and and_1 (out_5, w, not_1_out, y, not_2_out);
  not not_2 (not_2_out, z);
endmodule

module wx_yz (
  input  w,
  input  x,
  input  y,
  input  z,
  output out_5
);

  wire not_1_out, not_2_out;

  and and_1 (out_5, w, x, not_1_out, not_2_out);
  not not_1 (not_1_out, y);
  not not_2 (not_2_out, z);
endmodule

module wxy_z (
  input  w,
  input  x,
  input  y,
  input  z,
  output out_5
);

  and and_1 (out_5, w, x, y, z);
endmodule

module wxyz (
  input  w,
  input  x,
  input  y,
  input  z,
  output out_5
);

  and and_1 (out_5, w, x, y, z);
endmodule

module main1 (
  input  w,
  input  x,
  input  y,
  input  z,
  output out_5
);

  wire main_1_out_5, w_x_yz_1_out_5, w_xy_z_1_out_5, w_xyz_1_out_5, wx_y_z_1_out_5, wx_yz_1_out_5,
       wxy_z_1_out_5, wxyz_1_out_5;

  main main_1 (.w(w), .x(x), .y(y), .z(z), .out_5(main_1_out_5));
  w_x_yz w_x_yz_1 (.w(w), .x(x), .y(y), .z(z), .out_5(w_x_yz_1_out_5));
  w_xy_z w_xy_z_1 (.w(w), .x(x), .y(y), .z(z), .out_5(w_xy_z_1_out_5));
  w_xyz w_xyz_1 (.w(w), .x(x), .y(y), .z(z), .out_5(w_xyz_1_out_5));
  wx_y_z wx_y_z_1 (.w(w), .x(x), .y(y), .z(z), .out_5(wx_y_z_1_out_5));
  wx_yz wx_yz_1 (.w(w), .x(x), .y(y), .z(z), .out_5(wx_yz_1_out_5));
  wxy_z wxy_z_1 (.w(w), .x(x), .y(y), .z(z), .out_5(wxy_z_1_out_5));
  wxyz wxyz_1 (.w(w), .x(x), .y(y), .z(z), .out_5(wxyz_1_out_5));
  or or_1 (out_5, main_1_out_5, w_x_yz_1_out_5, w_xy_z_1_out_5, w_xyz_1_out_5, wx_y_z_1_out_5, wx_yz_1_out_5, wxy_z_1_out_5, wxyz_1_out_5);
endmodule
