// Logisim project 1801042673 lab2.circ as structural Verilog: 2 circuits, main circuit main
module circuit (
  input  W,
  input  X,
  input  Y,
  input  Z,
  output F1,
  output F2
);

  wire not_1_out, not_2_out, not_3_out;

  not not_1 (not_1_out, X);
  not not_2 (not_2_out, Y);
  not not_3 (not_3_out, Z);
  and and_1 (F1, not_1_out, not_3_out);
  and and_2 (F2, not_1_out, not_2_out);
endmodule

module main (
  input  W,
  input  X,
  input  Y,
  input  Z,
  output F1,
  output F2
);

  circuit circuit_1 (.W(W), .X(X), .Y(Y), .Z(Z), .F1(F1), .F2(F2));
endmodule
