// Logisim project lab3.circ as structural Verilog: 5 circuits, main circuit main
module main (
  input  A,
  input  B,
  input  C,
  input  D,
  input  E,
  output out_6
);

  wire a_b_ce_1_out_5, a_b_xnor_c_xnor_d_xnor_e_1_out_6, b_a_xnor_c_xnor_d_xnor_e_1_out_6, b_cde_1_out_5;

  A_B_XNOR_C_XNOR_D_XNOR_E a_b_xnor_c_xnor_d_xnor_e_1 (
    .in_1(A), .in_2(B), .in_3(C), .in_4(D), .in_5(E), .out_6(a_b_xnor_c_xnor_d_xnor_e_1_out_6));
  B_A_XNOR_C_XNOR_D_XNOR_E b_a_xnor_c_xnor_d_xnor_e_1 (
    .in_1(A), .in_2(B), .in_3(C), .in_4(D), .in_5(E), .out_6(b_a_xnor_c_xnor_d_xnor_e_1_out_6));
  B_CDE b_cde_1 (.B(B), .C(C), .D(D), .E(E), .out_5(b_cde_1_out_5));
  A_B_CE a_b_ce_1 (.A(A), .B(B), .C(C), .E(E), .out_5(a_b_ce_1_out_5));
  or or_1 (out_6, a_b_xnor_c_xnor_d_xnor_e_1_out_6, b_a_xnor_c_xnor_d_xnor_e_1_out_6, b_cde_1_out_5, a_b_ce_1_out_5);
endmodule

module B_CDE (
  input  B,
  input  C,
  input  D,
  input  E,
  output out_5
);

  wire not_1_out;

  not not_1 (not_1_out, B);
  and and_1 (out_5, not_1_out, C, D, E);
endmodule

module A_B_CE (
  input  A,
  input  B,
  input  C,
  input  E,
  output out_5
);

  wire not_1_out, not_2_out;

  not not_1 (not_1_out, A);
  not not_2 (not_2_out, B);
  and and_1 (out_5, not_1_out, not_2_out, C, E);
endmodule

module A_B_XNOR_C_XNOR_D_XNOR_E (
  input  in_1,
  input  in_2,
  input  in_3,
  input  in_4,
  input  in_5,
  output out_6
);

  wire xnor_1_out;

  NotExactlyOne xnor_1 (.out(xnor_1_out), .in0(in_2), .in1(in_3), .in2(in_4), .in3(in_5));
  and and_1 (out_6, in_1, xnor_1_out);
endmodule

module B_A_XNOR_C_XNOR_D_XNOR_E (
  input  in_1,
  input  in_2,
  input  in_3,
  input  in_4,
  input  in_5,
  output out_6
);

  wire xnor_1_out;

  NotExactlyOne xnor_1 (.out(xnor_1_out), .in0(in_1), .in1(in_3), .in2(in_4), .in3(in_5));
  and and_1 (out_6, in_2, xnor_1_out);
endmodule
