// Logisim project lab4.circ as structural Verilog: 3 circuits, main circuit main
module main (
  input  in_1,
  input  in_2,
  output out_3
);

  wire clock_1_out, combinational_circuit_1_n0, combinational_circuit_1_n1, n2_bit_register_1_r0,
       n2_bit_register_1_r1;

  Clock clock_1 (.out(clock_1_out));
  _2_bit_register u_2_bit_register_1 (
    .clock(clock_1_out), .N0(combinational_circuit_1_n0), .N1(combinational_circuit_1_n1),
    .R0(n2_bit_register_1_r0), .R1(n2_bit_register_1_r1));
  combinational_circuit combinational_circuit_1 (
    .R0(n2_bit_register_1_r0), .R1(n2_bit_register_1_r1), .a(in_1), .b(in_2), .x(out_3),
    .N0(combinational_circuit_1_n0), .N1(combinational_circuit_1_n1));
endmodule

module _2_bit_register (
  input  clock,
  input  N0,
  input  N1,
  output R0,
  output R1
);

  D_Flip_Flop d_ff_1 (.clk(clock), .D(N0), .Q(R0));  // open: Qn, preset, en, reset
  D_Flip_Flop d_ff_2 (.clk(clock), .D(N1), .Q(R1));  // open: Qn, preset, en, reset
endmodule

module combinational_circuit (
  input  R0,
  input  R1,
  input  a,
  input  b,
  output x,
  output N0,
  output N1
);

  wire and_1_out, and_2_out, and_3_out, and_4_out, and_5_out, and_6_out, not_1_out, not_2_out, not_3_out,
       not_4_out, not_5_out;

  not not_1 (not_1_out, R1);
  not not_2 (not_2_out, a);
  not not_3 (not_3_out, a);
  not not_4 (not_4_out, R0);
  not not_5 (not_5_out, b);
  and and_1 (and_1_out, R1, b);
  and and_2 (and_2_out, R0, b);
  and and_3 (and_3_out, R0, not_1_out, not_2_out);
  and and_4 (and_4_out, R0, not_3_out, b);
  and and_5 (and_5_out, R0, R1, b);
  and and_6 (and_6_out, not_4_out, a, not_5_out);
  or or_1 (N0, and_1_out, and_2_out, and_3_out);
  or or_2 (N1, and_4_out, and_5_out, and_6_out);

  assign x = R0;
endmodule
