// Logisim project lab5.circ as structural Verilog: 5 circuits, main circuit main
module main (
  input  req,
  input  p3s,
  input  p7s,
  input  p37s,
  output redL,
  output orangeL,
  output greenL,
  output resetT
);

  wire clock_1_out, combinational_part_1_n0, combinational_part_1_n1, n2_bit_register_1_r0,
       n2_bit_register_1_r1;

  Clock clock_1 (.out(clock_1_out));
  combinational_part combinational_part_1 (
    .req(req), .p3s(p3s), .p7s(p7s), .p37s(p37s), .R0(n2_bit_register_1_r0), .R1(n2_bit_register_1_r1),
    .redL(redL), .orangeL(orangeL), .greenL(greenL), .N0(combinational_part_1_n0),
    .N1(combinational_part_1_n1), .resetT(resetT));
  _2_bit_register u_2_bit_register_1 (
    .clock(clock_1_out), .N0(combinational_part_1_n0), .N1(combinational_part_1_n1),
    .R0(n2_bit_register_1_r0), .R1(n2_bit_register_1_r1));

  // Notes on the sheet:
  //   combinational part
  //   register
endmodule

module _2_bit_register (
  input  clock,
  input  N0,
  input  N1,
  output R0,
  output R1
);

  D_Flip_Flop d_ff_1 (.clk(clock), .D(N0), .Q(R0));  // open: Qn, preset, en, reset
  D_Flip_Flop d_ff_2 (.clk(clock), .D(N1), .Q(R1));  // open: Qn, preset, en, reset
endmodule

module combinational_part (
  input  req,
  input  p3s,
  input  p7s,
  input  p37s,
  input  R0,
  input  R1,
  output redL,
  output orangeL,
  output greenL,
  output N0,
  output N1,
  output resetT
);

  wire not_1_out, not_2_out, not_3_out, not_4_out;

  and and_1 (orangeL, R0, not_1_out);
  not not_1 (not_1_out, R1);
  and and_2 (greenL, R0, R1);
  N0_Simplified n0_simplified_1 (.R0(R0), .R1(R1), .p3s(p3s), .p37s(p37s), .N0(N0));
  N1_Simplified n1_simplified_1 (.req(req), .p3s(p3s), .p7s(p7s), .p37s(p37s), .R0(R0), .R1(R1), .N1(N1));
  not not_2 (not_2_out, p3s);
  and and_3 (resetT, not_2_out, not_3_out, not_4_out);
  not not_3 (not_3_out, p7s);
  not not_4 (not_4_out, p37s);
  not not_5 (redL, R0);

  // Notes on the sheet:
  //   N0
  //   N1
endmodule

module N0_Simplified (
  input  R0,
  input  R1,
  input  p3s,
  input  p37s,
  output N0
);

  wire and_1_out, and_2_out, and_3_out, not_1_out, not_2_out;

  not not_1 (not_1_out, R0);
  and and_1 (and_1_out, not_1_out, R1, p3s);
  and and_2 (and_2_out, R0, not_2_out);
  not not_2 (not_2_out, R1);
  and and_3 (and_3_out, R0, R1, p37s);
  or or_1 (N0, and_1_out, and_2_out, and_3_out);
endmodule

module N1_Simplified (
  input  req,
  input  p3s,
  input  p7s,
  input  p37s,
  input  R0,
  input  R1,
  output N1
);

  wire and_1_out, and_2_out, and_3_out, and_4_out, not_1_out, not_2_out, not_3_out, not_4_out, not_5_out,
       not_6_out;

  not not_1 (not_1_out, R0);
  not not_2 (not_2_out, R1);
  and and_1 (and_1_out, not_1_out, not_2_out, req);
  not not_3 (not_3_out, R0);
  and and_2 (and_2_out, not_3_out, R1, not_4_out);
  not not_4 (not_4_out, p3s);
  not not_5 (not_5_out, R1);
  and and_3 (and_3_out, R0, not_5_out, p7s);
  and and_4 (and_4_out, R0, R1, not_6_out);
  not not_6 (not_6_out, p37s);
  or or_1 (N1, and_1_out, and_2_out, and_3_out, and_4_out);
endmodule
