// Logisim project lab6.circ as structural Verilog: 1 circuit, main circuit datapath
module datapath (
  input  [7:0] in_1,
  input  [7:0] in_2,
  input  [7:0] in_3,
  input  ld_diff,
  input  [7:0] in_5,
  input  ld_diff2,
  input  [7:0] in_7,
  input  diff_decrement,
  input  [7:0] in_9,
  input  ld_z,
  output diff___0,
  output diff___10,
  output [7:0] out_13
);

  wire [7:0] adder_1_out, adder_2_out, multiplexer_1_out, multiplexer_2_out, register_1_q, register_2_q,
       subtractor_1_out, subtractor_2_out;

  Subtractor subtractor_1 (.a(in_1), .b(in_2), .out(subtractor_1_out));  // open: bin, bout
  Multiplexer #(.width(8)) multiplexer_1 (
    .in0(subtractor_1_out), .in1(subtractor_2_out), .out(multiplexer_1_out), .sel(diff_decrement));  // open: en
  Multiplexer #(.width(8)) multiplexer_2 (
    .in0(adder_1_out), .in1(adder_2_out), .out(multiplexer_2_out), .sel(diff___10));  // open: en
  Register register_1 (.D(multiplexer_1_out), .en(ld_diff), .Q(register_1_q));  // open: clk, clr
  Register register_2 (.D(register_1_q), .en(ld_diff2), .Q(register_2_q));  // open: clk, clr
  Register register_3 (.D(multiplexer_2_out), .en(ld_z), .Q(out_13));  // open: clk, clr
  Comparator comparator_1 (.a(register_1_q), .b(in_3), .gt(diff___0));  // open: eq, lt
  Comparator comparator_2 (.a(register_1_q), .b(in_5), .gt(diff___10));  // open: eq, lt
  Subtractor subtractor_2 (.a(register_1_q), .b(in_7), .out(subtractor_2_out));  // open: bin, bout
  Adder adder_1 (.a(out_13), .b(register_2_q), .out(adder_1_out));  // open: cin, cout
  Adder adder_2 (.a(out_13), .b(in_9), .out(adder_2_out));  // open: cin, cout

  // Notes on the sheet:
  //   diff
  //   diff2
  //   z
  //   diff -= 1
  //   z + diff2
  //   z + 5
  //   z
endmodule
