// Logisim project circuit.circ as structural Verilog: 5 circuits, main circuit main
module main (
  input  [7:0] in_1,
  input  Bd,
  input  R,
  input  W,
  input  Bc,
  input  _1min,
  input  _2min,
  input  _3min,
  output _1sec_Alarm,
  output _2sec_Alarm,
  output _3sec_Alarm
);

  wire clock_1_out, clock_2_out, clock_3_out, d_ff_1_q, d_ff_2_q, d_ff_3_q, danger_1_out_6, n0_cir_1_out_7,
       n1_cir_1_out_8, n2_cir_1_out_6, not_1_out, not_2_out, not_3_out, not_4_out;

  Danger danger_1 (.in_1(in_1), .Bd(Bd), .R(R), .W(W), .Bc(Bc), .out_6(danger_1_out_6));
  Clock clock_1 (.out(clock_1_out));
  D_Flip_Flop d_ff_1 (.clk(clock_1_out), .D(n2_cir_1_out_6), .Q(d_ff_1_q));  // open: Qn, preset, en, reset
  Clock clock_2 (.out(clock_2_out));
  Clock clock_3 (.out(clock_3_out));
  D_Flip_Flop d_ff_2 (.clk(clock_2_out), .D(n1_cir_1_out_8), .Q(d_ff_2_q));  // open: Qn, preset, en, reset
  D_Flip_Flop d_ff_3 (.clk(clock_3_out), .D(n0_cir_1_out_7), .Q(d_ff_3_q));  // open: Qn, preset, en, reset
  N2_cir n2_cir_1 (
    .R2(d_ff_1_q), .R1(d_ff_2_q), .R0(d_ff_3_q), ._3min(_3min), .Dang(danger_1_out_6), .out_6(n2_cir_1_out_6));
  not not_1 (not_1_out, d_ff_2_q);
  not not_2 (not_2_out, d_ff_2_q);
  not not_3 (not_3_out, d_ff_3_q);
  not not_4 (not_4_out, d_ff_1_q);
  N1_cir n1_cir_1 (
    .R2(d_ff_1_q), .R1(d_ff_2_q), .R0(d_ff_3_q), ._1min(_1min), ._2min(_2min), ._3min(_3min),
    .Dang(danger_1_out_6), .out_8(n1_cir_1_out_8));
  and and_1 (_1sec_Alarm, d_ff_1_q, not_1_out, d_ff_3_q);
  and and_2 (_2sec_Alarm, d_ff_1_q, not_2_out, not_3_out);
  and and_3 (_3sec_Alarm, not_4_out, d_ff_2_q, d_ff_3_q);
  N0_cir n0_cir_1 (
    .R2(d_ff_1_q), .R1(d_ff_2_q), .R0(d_ff_3_q), ._2min(_2min), ._3min(_3min), .Dang(danger_1_out_6),
    .out_7(n0_cir_1_out_7));

  // Notes on the sheet:
  //   V
  //   dang circuitry
  //   N2 circuitry
  //   N1 circuitry
  //   N0 circuitry
endmodule

module Danger (
  input  [7:0] in_1,
  input  Bd,
  input  R,
  input  W,
  input  Bc,
  output out_6
);

  wire comparator_1_gt, not_1_out, not_2_out, not_3_out;

  Comparator #(.mode("unsigned")) comparator_1 (.a(in_1), .b(8'h14), .gt(comparator_1_gt));  // open: eq, lt
  not not_1 (not_1_out, Bd);
  not not_2 (not_2_out, R);
  not not_3 (not_3_out, Bc);
  and and_1 (out_6, comparator_1_gt, not_1_out, not_2_out, W, not_3_out);

  // Notes on the sheet:
  //   V
endmodule

module N2_cir (
  input  R2,
  input  R1,
  input  R0,
  input  _3min,
  input  Dang,
  output out_6
);

  wire and_1_out, and_2_out, and_3_out, and_4_out, not_1_out, not_2_out, not_3_out, not_4_out, not_5_out,
       not_6_out;

  not not_1 (not_1_out, R2);
  and and_1 (and_1_out, not_1_out, R1, R0, _3min, Dang);
  not not_2 (not_2_out, R1);
  and and_2 (and_2_out, R2, not_2_out, not_3_out, Dang);
  not not_3 (not_3_out, R0);
  not not_4 (not_4_out, R0);
  and and_3 (and_3_out, R2, R1, not_4_out, not_5_out, Dang);
  not not_5 (not_5_out, _3min);
  not not_6 (not_6_out, R1);
  and and_4 (and_4_out, R2, not_6_out, R0, Dang);
  or or_1 (out_6, and_1_out, and_2_out, and_3_out, and_4_out);
endmodule

module N1_cir (
  input  R2,
  input  R1,
  input  R0,
  input  _1min,
  input  _2min,
  input  _3min,
  input  Dang,
  output out_8
);

  wire and_1_out, and_2_out, and_3_out, and_4_out, and_5_out, and_6_out, not_1_out, not_2_out, not_3_out,
       not_4_out, not_5_out, not_6_out, not_7_out, not_8_out, not_9_out, not_10_out;

  not not_1 (not_1_out, R1);
  not not_2 (not_2_out, R2);
  not not_3 (not_3_out, _3min);
  not not_4 (not_4_out, R2);
  not not_5 (not_5_out, R1);
  not not_6 (not_6_out, R2);
  not not_7 (not_7_out, Dang);
  not not_8 (not_8_out, R0);
  not not_9 (not_9_out, R1);
  not not_10 (not_10_out, Dang);
  and and_1 (and_1_out, R2, not_1_out, R0, _2min);
  and and_2 (and_2_out, not_2_out, R1, not_3_out);
  and and_3 (and_3_out, not_4_out, not_5_out, R0, _1min);
  and and_4 (and_4_out, not_6_out, not_7_out);
  and and_5 (and_5_out, R1, not_8_out);
  and and_6 (and_6_out, not_9_out, not_10_out);
  or or_1 (out_8, and_1_out, and_2_out, and_3_out, and_4_out, and_5_out, and_6_out);
endmodule

module N0_cir (
  input  R2,
  input  R1,
  input  R0,
  input  _2min,
  input  _3min,
  input  Dang,
  output out_7
);

  wire and_1_out, and_2_out, and_3_out, and_4_out, and_5_out, not_1_out, not_2_out, not_3_out, not_4_out,
       not_5_out, not_6_out, not_7_out, not_8_out, not_9_out;

  not not_1 (not_1_out, R2);
  not not_2 (not_2_out, R1);
  and and_1 (and_1_out, not_1_out, not_2_out, Dang);
  not not_3 (not_3_out, R2);
  not not_4 (not_4_out, _3min);
  and and_2 (and_2_out, not_3_out, not_4_out, Dang);
  not not_5 (not_5_out, R0);
  and and_3 (and_3_out, R1, not_5_out, _3min, Dang);
  not not_6 (not_6_out, R1);
  not not_7 (not_7_out, R0);
  and and_4 (and_4_out, not_6_out, not_7_out, _2min, Dang);
  not not_8 (not_8_out, R1);
  and and_5 (and_5_out, not_8_out, R0, not_9_out, Dang);
  not not_9 (not_9_out, _2min);
  or or_1 (out_7, and_1_out, and_2_out, and_3_out, and_4_out, and_5_out);
endmodule
